# Fritzing sketch Wasserstand (saved by Fritzing 0.9.3b)
breadboards: 1

parts:
  Bauteil1 = Arduino Uno (Rev3)
  Bauteil2 = SRF05 Ultrasonic Rangefinder
  GLCD_128x1 = LCD screen
  S1 = Momentary Switch [package=ksa_sealed_tac_switch]
  S2 = Momentary Switch [package=ksa_sealed_tac_switch]
  RHT1 = Humidity and Temperature Sensor RHT03
  LCM1602_IIC1 = LCM1602 IIC [part_number="LCM1602 IIC" chip_label="LCM1602 IIC" package="DIP (Dual Inline) [THT]"]
  U2 = NodeMCU V1.0
  M1 = DC Motor
  KY-2 = Keyes Relay [package=THT]

nets:
  N1: Bauteil1.A4/SDA, LCM1602_IIC1.SDA
  N2: Bauteil1.A5/SCL, LCM1602_IIC1.SCL
  N3: Bauteil1.D10_PWM/SS, U2.D1
  N4: Bauteil1.D11_PWM/MOSI, U2.D2
  N5: Bauteil1.D2, S1.3
  N6: Bauteil1.D3_PWM, S2.3
  N7: Bauteil1.D4, KY-2.signal
  N8: Bauteil1.D5_PWM, Bauteil2.Echo
  N9: Bauteil1.D6_PWM, Bauteil2.Trig
  N10: Bauteil1.D7, RHT1.Data-signal
  3V3: Bauteil1.3V3, U2.Vin
  VCC: Bauteil1.5V, Bauteil2.VCC, RHT1.Vcc, LCM1602_IIC1.VCC, KY-2.power
  GND: Bauteil1.GND, Bauteil2.GND, S1.2, S2.2, RHT1.GND_2, LCM1602_IIC1.GND, U2.GND, KY-2.ground
  VSS: GLCD_128x1.VSS, LCM1602_IIC1.VSS
  VDD: GLCD_128x1.VDD, LCM1602_IIC1.VDD
  N11: GLCD_128x1.V0, LCM1602_IIC1.V0
  N12: GLCD_128x1.RS, LCM1602_IIC1.RS
  N13: GLCD_128x1.R/W, LCM1602_IIC1.RW
  N14: GLCD_128x1.E, LCM1602_IIC1.E
  N15: GLCD_128x1.DB0, LCM1602_IIC1.D0
  N16: GLCD_128x1.DB1, LCM1602_IIC1.D1
  N17: GLCD_128x1.DB2, LCM1602_IIC1.D2
  N18: GLCD_128x1.DB3, LCM1602_IIC1.D3
  N19: GLCD_128x1.DB4, LCM1602_IIC1.D4
  N20: GLCD_128x1.DB5, LCM1602_IIC1.D5
  N21: GLCD_128x1.DB6, LCM1602_IIC1.D6
  N22: GLCD_128x1.DB7, LCM1602_IIC1.D7
  N23: GLCD_128x1.LED+, LCM1602_IIC1.A
  N24: GLCD_128x1.LED-, LCM1602_IIC1.K
  N25: M1.pin_1, KY-2.C

notes:
  Temperatur + Feuchte
  Serial -> Parallelumsetzer
  16x2 Display
  AC
  Arduino Uno
  ESP8266 Webserver
  Relais 30A, Null auf Common+NormOpen
  Pumpe, Anschluss vereinfacht dargestellt
  DHT22, linke Buchse
  Feuchte + Temperatur
  Ultraschall Pegelmesser
  rechte Buchse
  Zwei Drucktaster zur
  Konfiguration
  Schaltplan - Farben stimmen mit Schaltung überein!

custom parts:
  LCM1602 IIC: I2C-Module to use a 1602 or 2004 LCD on with the wire.h libory Serial LCD Modul
  NodeMCU V1.0: ESP8266 based NodeMCU
  Keyes Relay: The Keyes 5V relay module is suitable for SCM development, home appliance control. It uses a 5V~12V TIL control signal which can control DC / AC signal.
